// Logisim project Ex5.8.circ as structural Verilog
module a__not_equal (
  input  [31:0] A,
  input  [31:0] B,
  output out_3
);

  Comparator #(.width(32)) comparator_1 (.a(A), .b(B), .eq(out_3));  // open: gt, lt
endmodule

module b__greater_than_or (
  input  [31:0] A,
  input  [31:0] B,
  output out_3
);

  wire comparator_1_eq, comparator_1_gt;

  Comparator #(.width(32)) comparator_1 (.a(A), .b(B), .gt(comparator_1_gt), .eq(comparator_1_eq));  // open: lt
  or or_1 (out_3, comparator_1_gt, comparator_1_eq);
endmodule

module c__less_than (
  input  [31:0] A,
  input  [31:0] B,
  output out_3
);

  Comparator #(.width(32)) comparator_1 (.a(A), .b(B), .lt(out_3));  // open: gt, eq
endmodule
